# Fritzing sketch Schematics (saved by Fritzing 0.9.4)
breadboards: 1

parts:
  WeMos_D1_Mini1 = WeMos D1 Mini
  M1 = RioRand LM2596
  SP1 = SPEAKER [part_number=Outside package=pcb_mount_speaker]
  Bell_Button = Round Pushbutton
  Siedle_Pin_I = male pin header, 1 pin [form="♂ (male)"]
  Siedle_Pin_c = male pin header, 1 pin [form="♂ (male)"]
  Connector = Screw terminal - 2 pins [package=THT]
  R1 = Resistor [tolerance=±5% resistance=1.2k package=THT]
  R2 = Resistor [tolerance=±5% resistance=1.2k package=THT]
  Q1 = NPN-Transistor [package="TO92 [THT]"]
  Door_Opener = Vibration Motor- ROB-08449 [package=vibe-motor-10mm]
  Bell = Piezo Speaker
  MIC1 = Microphone [part_number="Mic Outside"]
  SP2 = SPEAKER [part_number=Inside package=pcb_mount_speaker]
  MIC2 = Microphone [part_number="Mic Inside"]
  Siedle_Pin_11 = male pin header, 1 pin [form="♂ (male)"]
  Siedle_Pin_12 = male pin header, 1 pin [form="♂ (male)"]
  Hang_Switch = SWITCH-DPDT [package=es]
  Siedle_Pin_9 = male pin header, 1 pin [form="♂ (male)"]
  Door_Opener_Button = Round Pushbutton
  Buzzer = Piezo Speaker
  Siedle_Pin_7 = male pin header, 1 pin [form="♂ (male)"]
  D1 = bridge rectifier TO-269AA [package="TO-269AA [SMD]"]
  V1 = AC Power [voltage=12V frequency=60]  # not connected
  V2 = AC Power [voltage=7V frequency=60]
  U1 = MOC3031-M [part_number=MOC3041 package=dil06]
  D2 = Rectifier Diode [part_number=1N4001 package="300 mil [THT]"]

nets:
  N1: WeMos_D1_Mini1.5V, M1.Pin_3
  N2: WeMos_D1_Mini1.D1, Q1.C
  N3: WeMos_D1_Mini1.D2, R1.Pin_0
  AC-12V-2/GND: WeMos_D1_Mini1.G, M1.Pin_4, Bell_Button.leg0, Siedle_Pin_c.pin1, Q1.E, Door_Opener_Button.leg1, Buzzer.pin1, D1.AC#1, U1.2, U1.6
  N4: M1.Pin_1, D1.DC-
  N5: M1.Pin_2, D1.DC+
  N6: SP1.+, Hang_Switch.2
  AC-7V-1: SP1.-, MIC1.pin2, V2.V+
  Bell-button: Bell_Button.leg1, Connector.pin2, Bell.pin2, D2.anode
  Door opener: Siedle_Pin_I.pin1, Door_Opener.-, Door_Opener_Button.leg0, U1.4
  AC-12v-2: Connector.pin1, D1.AC#0
  N7: R1.Pin_1, U1.1
  N8: R2.Pin_0, D2.cathode
  N9: R2.Pin_1, Q1.B
  N10: Door_Opener.+, Bell.pin1
  Speaker: MIC1.pin1, Siedle_Pin_12.pin1, Hang_Switch.5
  N11: SP2.+, MIC2.pin2
  N12: SP2.-, Hang_Switch.4
  N13: MIC2.pin1, Hang_Switch.1
  MIC: Siedle_Pin_11.pin1
  AC-7V-2: Siedle_Pin_9.pin1, V2.V-
  Buzzer: Buzzer.pin2, Siedle_Pin_7.pin1

notes:
  Auto Opener Board
  Interphone Siedle HT401a - Home Phone
  External
